# Fritzing sketch Anthony_Jeriel_Photogate (saved by Fritzing 0.9.3b)
breadboards: 1

parts:
  Part1 = Arduino Due (Rev2b)
  R1 = Resistor [tolerance=±5% resistance=220 package="1206 [SMD]"]
  R2 = Resistor [tolerance=±5% resistance=220 package="1206 [SMD]"]
  LED1 = LEDs [package=led10mm]
  R3 = PHOTOCELL [package=photocell-kit]

nets:
  N1: Part1.A0, R1.Pin_0, R3.P$1
  N2: Part1.IOREF, Part1.GND, R2.Pin_1, LED1.A
  N3: R1.Pin_1, LED1.C
  N4: R2.Pin_0, R3.P$2
