# Fritzing sketch Anthony_Jeriel_Photoresistor (saved by Fritzing 0.9.3b)
breadboards: 1

parts:
  Part1 = Arduino Due (Rev2b)
  R1 = PHOTOCELL [package=photocell-kit]
  R2 = Resistor [tolerance=±5% resistance=220 package="0603 [SMD]"]

nets (from the schematic view):
  N1: Part1.A0, R1.P$1
  N2: Part1.IOREF, R1.P$2
  N3: Part1.GND, R2.Pin_0
