# Fritzing sketch Anthony_Jeriel_SoundGen (saved by Fritzing 0.9.3b)
breadboards: 1

parts:
  Part1 = Arduino Due (Rev2b)
  R1 = Resistor [tolerance=±5% resistance=220 package="0402 [SMD]"]
  MIC1 = Microphone

nets:
  N1: Part1.DAC0, R1.Pin_1
  N2: Part1.GND, MIC1.pin1
  N3: R1.Pin_0, MIC1.pin2
