# Fritzing sketch LED_Button_press (saved by Fritzing 0.9.3b)

parts:
  R1 = Resistor [tolerance=±5% resistance=10k package="0402 [SMD]"]
  Part1 = Arduino Due (Rev2b)
  S1 = Pushbutton [package="[SMD]"]
  R2 = Resistor [tolerance=±5% resistance=220 package="0402 [SMD]"]
  LED1 = smd LED [color="Red (633nm)" package="0603 [SMD]"]

nets:
  N1: R1.Pin_0, S1.Pin_3, S1.Pin_4
  N2: R1.Pin_1, Part1.GND, LED1.cathode
  N3: Part1.D3_PWM, Part1.5V, S1.Pin_1, S1.Pin_2
  N4: Part1.D5_PWM, R2.Pin_1
  N5: R2.Pin_0, LED1.anode
